# Fritzing sketch bonsaiaio_sketch (saved by Fritzing 0.9.3b)
breadboards: 3

parts:
  U1 = NodeMCU V3.0
  YwRobot_Power_Supply1 = YwRobot Breadboard Power Supply [part_number=545043]
  LCD1 = LCD screen
  R1 = Rotary Potentiometer (Small) [maximum_resistance=100kΩ package=THT]
  DHT1 = DHT11 Humitidy and Temperature Sensor
  Water_Level_Sensor1 = Water Level Sensor
  S1 = Pushbutton [package="[SMD]"]
  R2 = Resistor [tolerance=±5% resistance=220 package="0805 [SMD]"]

nets:
  N1: U1.D1, DHT1.VDD
  N2: U1.D2, LCD1.DB7
  N3: U1.D3, LCD1.DB6
  N4: U1.D4, LCD1.DB5
  3V3: U1.3V3, Water_Level_Sensor1.VCC
  GND: U1.GND, YwRobot_Power_Supply1.GND#13, LCD1.LED-, R1.leg2, DHT1.GND, Water_Level_Sensor1.GND, R2.Pin_1
  N5: U1.D5, LCD1.DB4
  N6: U1.D6, LCD1.E
  N7: U1.D7, LCD1.RS
  N8: U1.RX, S1.Pin_1, S1.Pin_2, R2.Pin_0
  N9: U1.Vin, YwRobot_Power_Supply1.VCC#9, R1.leg1, DHT1.DATA, S1.Pin_3, S1.Pin_4
  N10: U1.A0, Water_Level_Sensor1.SIG
  N11: LCD1.LED+, R1.wiper

custom parts:
  NodeMCU V3.0: NodeMcu V3 Lua WIFI Development Board
  YwRobot Breadboard Power Supply: The YwRobot Breadboard Power Supply (MB-V2) has two power rails; they can be 5V or 3V3. Power to the module can be provided through the female USB socket or through the A10 (female) 2.1mm power jack.
  DHT11 Humitidy and Temperature Sensor: DHT11 Humidity and Temperature Sensor
  Water Level Sensor: A water level sensor. This sensor operates at 3V to 5V. The Sig (signal) pin outputs an analogue signal that is in proportion to the amount of water in contact with the sensor.
